# Fritzing sketch windows_volume_mixer (saved by Fritzing 0.9.6b)

parts:
  Part1 = Adafruit I2C QT Rotary Encoder [part_number="Adafruit #4991"]
  Part2 = Adafruit I2C QT Rotary Encoder [part_number="Adafruit #4991"]
  Part3 = Adafruit I2C QT Rotary Encoder [part_number="Adafruit #4991"]
  Part4 = Adafruit I2C QT Rotary Encoder [part_number="Adafruit #4991"]
  OLED_I2C1 = OLED 128x64 I2C Monochrome Display
  OLED_I2C2 = OLED 128x64 I2C Monochrome Display  # not connected
  OLED_I2C3 = OLED 128x64 I2C Monochrome Display
  OLED_I2C4 = OLED 128x64 I2C Monochrome Display  # not connected
  Part5 = Adafruit Feather RP2040 [part_number="Adafruit #4884"]
  Part6 = 16 NeoPixel Ring [part_number=1463]
  Part7 = 16 NeoPixel Ring [part_number=1463]
  Part8 = 16 NeoPixel Ring [part_number=1463]
  Part9 = 16 NeoPixel Ring [part_number=1463]
  Part10 = Adafruit NeoKey 1x4 QT I2C [part_number="adafruit #4980"]
  Part11 = Adafruit NeoKey 1x4 QT I2C [part_number="adafruit #4980"]
  Part12 = Adafruit FeatherWing Proto [part_number="Adafruit #2884"]
  J1 = JST-03JQ-BT [part_number=JST-JQ-BT package=THT]
  J2 = JST-03JQ-BT [part_number=JST-JQ-BT package=THT]
  J3 = JST-03JQ-BT [part_number=JST-JQ-BT package=THT]
  J4 = JST-03JQ-BT [part_number=JST-JQ-BT package=THT]
  J5 = JST-03JQ-BT [part_number=JST-JQ-BT package=THT]
  J6 = JST-03JQ-BT [part_number=JST-JQ-BT package=THT]
  J8 = JST-03JQ-BT [part_number=JST-JQ-BT package=THT]
  J9 = JST-03JQ-BT [part_number=JST-JQ-BT package=THT]
  J10 = JST-03JQ-BT [part_number=JST-JQ-BT package=THT]
  J7 = JST-03JQ-BT [part_number=JST-JQ-BT package=THT]

nets:
  GND: Part1.GND, Part2.GND, Part3.GND, Part4.GND, OLED_I2C1.GND, Part5.GND, Part10.GND, Part11.GND
  VCC: Part1.VCC, Part2.VCC, Part3.VCC, Part4.VCC, OLED_I2C1.VDD, Part5.+3V3, Part10.VCC, Part11.VCC
  N1: Part1.SDA, Part2.SDA, Part3.SDA, Part4.SDA, OLED_I2C1.SDA, Part5.SDA, Part10.SDA, Part11.SDA
  N2: Part1.SCL, Part2.SCL, Part3.SCL, Part4.SCL, OLED_I2C1.SCK, Part5.SCL, Part10.SCL, Part11.SCL
  N3: OLED_I2C3.SDA, J9.pin1
  N4: OLED_I2C3.SCK, J9.pin2
  N5: OLED_I2C3.VDD, J9.pin3
  N6: Part6.IN, J8.pin3
  N7: Part6.GND, J8.pin1
  N8: Part6.VDD, J8.pin2
  N9: Part7.IN, J5.pin3
  N10: Part7.GND, J5.pin1
  N11: Part7.VDD, J5.pin2
  N12: Part8.IN, J6.pin3
  N13: Part8.GND, J6.pin1
  N14: Part8.VDD, J6.pin2
  N15: Part9.IN, J7.pin3
  N16: Part9.GND, J7.pin1
  N17: Part9.VDD, J7.pin2
  N18: Part12.K, Part12.N$133, J10.pin2
  N19: Part12.J, Part12.N$124, J10.pin1
  N20: Part12.D, Part12.N$112, J4.pin3
  N21: Part12.C, Part12.N$95, J3.pin3
  N22: Part12.B, Part12.N$80, J2.pin3
  N23: Part12.A, Part12.N$69, J1.pin3
  N24: Part12.GND, Part12.N$67, Part12.N$82, Part12.N$97, Part12.N$131, J1.pin1, J2.pin1, J3.pin1
  N25: Part12.3V, Part12.N$68, Part12.N$83, Part12.N$96, Part12.N$111, Part12.N$132, J1.pin2, J2.pin2, J3.pin2, J4.pin2, J10.pin3
  N26: Part12.N$110, J4.pin1

custom parts:
  Adafruit I2C QT Rotary Encoder: Rotary encoders are soooo much fun! Twist em this way, then twist them that way. Unlike potentiometers, they go all the way around, and often have little detents for tactile feedback. But, if you've ever tried to add encoders to your project you know that they're a real challenge to use: timers, interrupts, debouncing... This Stemma QT breakout makes all that frustration go away - solder in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
  Adafruit Feather RP2040: A new chip means a new Feather, and the Raspberry Pi RP2040 is no exception. When we saw this chip we thought "this chip is going to be awesome when we give it the Feather Treatment" and so we did! This Feather features the RP2040, and all niceties you know and love about Feather Measures 2.0" x 0.9" x 0.28" (50.8mm x 22.8mm x 7mm) without headers soldered in Light as a (large?) feather - 5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
  16 NeoPixel Ring: 16 ultra bright smart LED NeoPixels are arranged in a circle with 1.75" (44.5mm) outer diameter. The rings are 'chainable' - connect the output pin of one to the input pin of another. Use only one microcontroller pin to control as many as you can chain together! Each LED is addressable as the driver chip is inside the LED. Each one has ~18mA constant current drive so the color will be very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
  Adafruit NeoKey 1x4 QT I2C: The only thing better than a nice mechanical key is, perhaps, FOUR mechanical keys that also can glow any color of the rainbow - and that's what the Adafruit NeoKey 1x4 QT I2C Breakout will let you do! This longgg 3" x 0.8" PCB fits four Cherry MX or compatible switches and make it easy to use with a breadboard/perfboard or with a STEMMA QT (Qwiic) connector for instant I2C connectivity on any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
  Adafruit FeatherWing Proto: This is the FeatherWing Proto - a prototyping add-on for all Feather boards. Using our Feather Stacking Headers or Feather Female Headers you can connect a FeatherWing on top or bottom of your Feather board and let the board take flight! This has a duplicate breakout for each pin on a Feather, as well as a bunch of plain grid proto holes. For GND and 3.3V, we give you a strip of connected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
